// Logisim project mips.circ as structural Verilog: 4 circuits, main circuit main
module main (
);

  wire clock_1_out, control_unit_1_alusrc, control_unit_1_outsrc, control_unit_1_regwr, Reset_PC_out;
  wire [4:0] multiplexer_2_out;
  wire [5:0] control_unit_1_aluop;
  wire [23:0] adder_1_out, pc_q;
  wire [31:0] alu_1_output, demultiplexer_1_out0, demultiplexer_1_out8, demultiplexer_1_out9,
       demultiplexer_1_out10, multiplexer_1_out, multiplexer_3_out, multiplexer_4_out, ram_1_data,
       sign_extend_1__32bit, t0_q, t1_q, t2_q, zero_q;

  Button Reset_PC (.out(Reset_PC_out));
  Register #(.width(24)) pc (.D(adder_1_out), .Q(pc_q), .clk(clock_1_out), .clr(Reset_PC_out));  // open: en
  Clock clock_1 (.out(clock_1_out));
  Adder #(.width(24)) adder_1 (.a(24'h1), .b(pc_q), .out(adder_1_out));  // open: cin, cout
  RAM #(.addrWidth(24), .dataWidth(32)) ram_1 (
    .addr(pc_q), .data(ram_1_data), .clk(clock_1_out));  // open: sel, ld, clr
  RAM ram_2 ();  // open: addr, data, sel, clk, ld, clr
  Control_Unit control_unit_1 (
    .Instruction(ram_1_data), .RegWr(control_unit_1_regwr), .ALUSrc(control_unit_1_alusrc),
    .OutSrc(control_unit_1_outsrc), .ALUOp(control_unit_1_aluop));  // open: MemRd, MemWr, Branch
  Sign_Extend sign_extend_1 (._16bit(ram_1_data[15:0]), ._32bit(sign_extend_1__32bit));
  Register #(.width(32)) zero (
    .D(demultiplexer_1_out0), .en(control_unit_1_regwr), .Q(zero_q), .clk(clock_1_out), .clr(Reset_PC_out));
  Register #(.width(32)) t0 (
    .D(demultiplexer_1_out8), .en(control_unit_1_regwr), .Q(t0_q), .clk(clock_1_out), .clr(Reset_PC_out));
  Register #(.width(32)) t1 (
    .D(demultiplexer_1_out9), .en(control_unit_1_regwr), .Q(t1_q), .clk(clock_1_out), .clr(Reset_PC_out));
  Register #(.width(32)) t2 (
    .D(demultiplexer_1_out10), .en(control_unit_1_regwr), .Q(t2_q), .clk(clock_1_out), .clr(Reset_PC_out));
  Multiplexer #(.select(5), .width(32)) multiplexer_1 (
    .in0(zero_q), .in8(t0_q), .in9(t1_q), .in10(t2_q), .out(multiplexer_1_out), .sel(ram_1_data[25:21]),
    .en(control_unit_1_regwr));  // open: in1, in2, in3, in4, in5, in6, in7, in11, in12, in13, in14, in15, in16, in17, in18, in19, in20, in21, in22, in23, in24, in25, in26, in27, in28, in29, in30, in31
  Multiplexer #(.width(5)) multiplexer_2 (
    .in0(ram_1_data[15:11]), .in1(ram_1_data[20:16]), .out(multiplexer_2_out), .sel(control_unit_1_outsrc),
    .en(control_unit_1_regwr));
  Multiplexer #(.select(5), .width(32)) multiplexer_3 (
    .in0(zero_q), .in8(t0_q), .in9(t1_q), .in10(t2_q), .out(multiplexer_3_out), .sel(ram_1_data[20:16]),
    .en(control_unit_1_regwr));  // open: in1, in2, in3, in4, in5, in6, in7, in11, in12, in13, in14, in15, in16, in17, in18, in19, in20, in21, in22, in23, in24, in25, in26, in27, in28, in29, in30, in31
  Multiplexer #(.width(32)) multiplexer_4 (
    .in0(sign_extend_1__32bit), .in1(multiplexer_3_out), .out(multiplexer_4_out),
    .sel(control_unit_1_alusrc), .en(control_unit_1_regwr));
  ALU alu_1 (.rs(multiplexer_1_out), .rt___I(multiplexer_4_out), .ALU_op(control_unit_1_aluop), .Output(alu_1_output));
  Demultiplexer #(.select(5), .width(32)) demultiplexer_1 (
    .out0(demultiplexer_1_out0), .out8(demultiplexer_1_out8), .out9(demultiplexer_1_out9),
    .out10(demultiplexer_1_out10), .in(alu_1_output), .sel(multiplexer_2_out), .en(control_unit_1_regwr));  // open: out1, out2, out3, out4, out5, out6, out7, out11, out12, out13, out14, out15, out16, out17, out18, out19, out20, out21, out22, out23, out24, out25, out26, out27, out28, out29, out30, out31

  // Notes on the sheet:
  //   R
  //   I
  //   rs
  //   rt
endmodule

module ALU (
  input  [31:0] rs,
  input  [31:0] rt___I,
  input  [5:0] ALU_op,
  output [31:0] Output
);

  wire [31:0] adder_1_out, and_1_out, nor_1_out, or_1_out, subtractor_1_out;

  Adder #(.width(32)) adder_1 (.a(rs), .b(rt___I), .out(adder_1_out));  // open: cin, cout
  Subtractor #(.width(32)) subtractor_1 (.a(rs), .b(rt___I), .out(subtractor_1_out));  // open: bin, bout
  assign and_1_out = rs & rt___I;  // AND_Gate and_1, 32 bits wide
  assign or_1_out = rs | rt___I;  // OR_Gate or_1, 32 bits wide
  assign nor_1_out = ~(rs | rt___I);  // NOR_Gate nor_1, 32 bits wide
  Multiplexer #(.select(5), .width(32)) multiplexer_1 (
    .in0(adder_1_out), .in2(subtractor_1_out), .in4(and_1_out), .in5(or_1_out), .in7(nor_1_out),
    .out(Output), .sel(ALU_op[4:0]), .en(ALU_op[5]));  // open: in1, in3, in6, in8, in9, in10, in11, in12, in13, in14, in15, in16, in17, in18, in19, in20, in21, in22, in23, in24, in25, in26, in27, in28, in29, in30, in31

  // Notes on the sheet:
  //   100000 - add
  //   100100 - and
  //   100101 - or
  //   100010 - sub
  //   100111 - nor
endmodule

module Control_Unit (
  input  [31:0] Instruction,
  output RegWr,
  output MemRd,
  output ALUSrc,
  output MemWr,
  output OutSrc,
  output Branch,
  output [5:0] ALUOp
);

  wire or_1_out;
  wire [5:0] rom_2_data;

  or or_1 (or_1_out, Instruction[26], Instruction[27], Instruction[28], Instruction[29], Instruction[30], Instruction[31]);
  ROM #(.addrWidth(6), .dataWidth(6)) rom_1 (
    .addr(Instruction[31:26]), .data({Branch, OutSrc, MemWr, ALUSrc, MemRd, RegWr}));  // open: sel
  ROM #(.addrWidth(6), .dataWidth(6)) rom_2 (.addr(Instruction[31:26]), .data(rom_2_data));  // open: sel
  Multiplexer #(.width(6), .enable("false")) multiplexer_1 (
    .in0(Instruction[31:26]), .in1(rom_2_data), .out(ALUOp), .sel(or_1_out));

  // Notes on the sheet:
  //   contents of rom_1 (hex, n*v repeats v):
  //   22 7*0 11
  //   contents of rom_2 (hex, n*v repeats v):
  //   8*0 20
endmodule

module Sign_Extend (
  input  [15:0] _16bit,
  output [31:0] _32bit
);


  assign _32bit = {{17{_16bit[15]}}, _16bit[14:0]};
endmodule
